// Logisim project Example 1.circ as structural Verilog: 1 circuit, main circuit main
module main (
  input  A,
  input  B,
  input  B_2,
  output F
);

  wire and_1_out, and_2_out, and_3_out, not_1_out, not_2_out, not_3_out, not_4_out, not_5_out;

  not not_1 (not_1_out, A);
  not not_2 (not_2_out, B);
  not not_3 (not_3_out, B_2);
  not not_4 (not_4_out, A);
  not not_5 (not_5_out, B_2);
  and and_1 (and_1_out, not_1_out, not_2_out, not_3_out);
  and and_2 (and_2_out, not_4_out, B, B_2);
  and and_3 (and_3_out, A, B, not_5_out);
  or or_1 (F, and_1_out, and_2_out, and_3_out);

  // Notes on the sheet:
  //   F(ABC) =A'B'C' +A'BC +ABC'
  //   Example One
endmodule
