// Logisim project Lab 4.circ as structural Verilog: 1 circuit, main circuit main
module main (
  input  A,
  input  B,
  input  C,
  output F
);

  wire and_1_out, and_2_out, and_3_out, and_4_out, not_1_out, not_2_out, not_3_out;

  not not_1 (not_1_out, A);
  not not_2 (not_2_out, B);
  not not_3 (not_3_out, C);
  and and_1 (and_1_out, not_1_out, B, C);
  and and_2 (and_2_out, A, not_2_out, C);
  and and_3 (and_3_out, A, B, not_3_out);
  and and_4 (and_4_out, A, B, C);
  or or_1 (F, and_1_out, and_2_out, and_3_out, and_4_out);

  // Notes on the sheet:
  //   E00942993
  //   COSC 221 Sec 0
  //   Lab #4
  //   Michael Masterson
  //   October 9, 2014
  //   F(A,B,C) =A'BC+AB'C+ABC' +ABC
  //   Function that generated in a combinational circuit when the output is equal to 1 if the input variables have more 1's than 0's. The output is 0, otherwise
endmodule
