// Logisim project Lab 5.circ as structural Verilog: 1 circuit, main circuit main
module main (
  input  A0,
  input  B0,
  input  A1,
  input  B1,
  output G,
  output E,
  output L
);

  wire and_1_out, and_2_out, and_3_out, and_4_out, and_5_out, and_6_out, and_7_out, and_8_out, and_9_out,
       and_11_out, not_1_out, not_2_out, not_3_out, not_4_out, not_5_out, not_6_out, not_7_out, not_8_out,
       or_1_out, or_2_out;

  not not_1 (not_1_out, A0);
  not not_2 (not_2_out, B0);
  not not_3 (not_3_out, A0);
  not not_4 (not_4_out, B1);
  not not_5 (not_5_out, A1);
  not not_6 (not_6_out, B1);
  not not_7 (not_7_out, A1);
  not not_8 (not_8_out, B0);
  and and_1 (and_1_out, A1, not_4_out);
  and and_2 (and_2_out, not_5_out, not_6_out);
  and and_3 (and_3_out, A1, B1);
  and and_4 (and_4_out, not_7_out, B1);
  and and_5 (and_5_out, A0, not_8_out);
  and and_6 (and_6_out, not_1_out, not_2_out);
  and and_7 (and_7_out, A0, B0);
  and and_8 (and_8_out, not_3_out, B0);
  or or_1 (or_1_out, and_6_out, and_7_out);
  or or_2 (or_2_out, and_2_out, and_3_out);
  and and_9 (and_9_out, and_5_out, or_2_out);
  and and_10 (E, or_1_out, or_2_out);
  or or_3 (G, and_9_out, and_1_out);
  and and_11 (and_11_out, and_8_out, or_2_out);
  or or_4 (L, and_4_out, and_11_out);

  // Notes on the sheet:
  //   Lab #5
  //   Fall 2014
  //   Michael Masterson
  //   E00942992
  //   COSC 221 sec. 0
  //   October 20, 2014
  //   G0=A>B
  //   L0=A<B
  //   G1
  //   L1
  //   E0=A=B
  //   E1
  //   Using a 1 bit comparator, construct a 2 bit comparator that compares two unsigned 2 bit inputs A and B and sserts the outputs to G,E,L depending on if A>B,A=B, and A<B
  //   E= E1*E0
  //   G=G1+(E1*G0)
  //   L = L1+(E1*L0)
endmodule
