// Logisim project combinational circuits 2.circ as structural Verilog: 1 circuit, main circuit main
module main (
  input  in_1,
  input  in_2,
  input  in_3,
  input  in_4,
  input  in_5,
  input  in_6,
  input  in_7,
  input  in_8,
  input  in_9,
  input  in_10,
  input  in_11,
  input  in_12,
  input  in_13,
  input  in_14,
  input  Enabler,
  input  [1:0] in_16,
  output out_17,
  output out_18,
  output sum,
  output out_20,
  output out_21,
  output out_22,
  output out_23,
  output out_24,
  output out_25,
  output out_26,
  output out_27,
  output out_28
);

  Comparator #(.width(1)) comparator_1 (.a(in_12), .b(in_13), .gt(out_20), .eq(out_21), .lt(out_22));
  Decoder #(.enable("false")) decoder_1 (.out0(out_24), .out1(out_26), .sel(in_14));
  Multiplexer #(.enable("false")) multiplexer_1 (.in0(in_3), .in1(in_7), .out(out_18), .sel(in_9));
  Decoder #(.select(2)) decoder_2 (
    .out0(out_23), .out1(out_25), .out2(out_27), .out3(out_28), .sel(in_16), .en(Enabler));
  Multiplexer multiplexer_2 (.in0(in_1), .in1(in_2), .out(out_17), .sel(in_4), .en(in_5));
  Adder #(.width(1)) adder_1 (.a(in_8), .b(in_10), .out(sum), .cin(in_6), .cout(in_11));

  // Notes on the sheet:
  //   Without enable
  //   Without enable
  //   with enable
  //   carry out
endmodule
